# Fritzing sketch TTGO800L_SchematicDiag01062024 (saved by Fritzing 0.9.3b)
circuit board: 10.3619cm x 7.84374cm
breadboards: 1

parts:
  Part1 = u-blox NEO-6M GPS Breakout
  Mod1 = TTGO-T-Call-V1.3-ESP32 [package=THT]

nets:
  GND: Part1.GND, Mod1.GND
  VCC: Part1.VCC, Mod1.3V3
  N1: Part1.TXD, Mod1.TXD
  N2: Part1.RXD, Mod1.RXD

notes:
  FOR FINAL DESIGN:
  USE MALE-TO-MALE WIRING FOR GPS TO ESEP32

custom parts:
  TTGO-T-Call-V1.3-ESP32: LILYGO® TTGO T-Call V1.3 ESP32 Wireless Module GPRS Antenna SIM Card SIM800L Module
